// Logisim project ULA+Teclado.circ as structural Verilog: 1 circuit, main circuit main
// zera
module main (
  input  in_1,
  input  in_2,
  input  in_3,
  input  in_4,
  input  in_5,
  input  in_6,
  output [6:0] out_7,
  output [6:0] out_8,
  output out_9
);

  wire a1, and_2_out, and_3_out, and_4_out, and_5_out, \botão_1 , clock_1_out, clock_2_out, comparator_1_eq,
       comparator_2_eq, comparator_3_eq, comparator_4_eq, comparator_5_eq, comparator_6_eq, contador_ram,
       load, not_1_out, or_3_out, register_1_q, verifica_oi, zera, zera_oi;
  wire [1:0] counter_3_q;
  wire [2:0] counter_1_q, counter_2_q, teste;
  wire [6:0] buffer_1_out, multiplexer_1_out, oi, \output , rom_1_data, rom_2_data, saidaRam2;

  Keyboard keyboard_1 (.clk(\botão_1 ), .re(in_5), .clr(in_2), .avail(a1), .data(out_8));
  Clock clock_1 (.out(clock_1_out));
  Comparator #(.width(7)) comparator_1 (.a(out_8), .b(7'b0001010), .eq(comparator_1_eq));  // open: gt, lt
  Comparator #(.width(7)) comparator_2 (.a(\output ), .b(7'b0001010), .eq(comparator_2_eq));  // open: gt, lt
  and and_1 (\botão_1 , in_5, clock_1_out);
  Multiplexer #(.width(7), .enable("false")) multiplexer_1 (
    .in0(out_8), .in1(oi), .out(multiplexer_1_out), .sel(verifica_oi));
  assign buffer_1_out = out_8;  // Buffer buffer_1, 7 bits wide
  not not_1 (not_1_out, in_5);
  D_Flip_Flop d_ff_1 (.clk(comparator_1_eq), .D(comparator_1_eq), .Q(load), .reset(zera));  // open: Qn, preset, en
  and and_2 (and_2_out, comparator_2_eq, verifica_oi);
  TTY tty_1 (.data(multiplexer_1_out), .clk(\botão_1 ), .we(\botão_1 ), .clr(in_3));
  or or_1 (contador_ram, not_1_out, zera);
  Counter #(.width(3), .max('h3)) counter_1 (
    .load(in_4), .Q(counter_1_q), .clk(\botão_1 ), .clr(zera));  // open: D, count, carry
  D_Flip_Flop d_ff_2 (.clk(and_2_out), .D(and_2_out), .Q(out_9), .reset(zera));  // open: Qn, preset, en
  Counter #(.width(3), .max('h3)) counter_2 (
    .load(in_1), .Q(counter_2_q), .clk(\botão_1 ), .clr(contador_ram));  // open: D, count, carry
  RAM #(.addrWidth(3), .dataWidth(7), .bus("separate")) ram_1 (
    .addr(counter_2_q), .din(buffer_1_out), .data(out_7), .str(a1), .clk(\botão_1 ), .ld(load),
    .clr(contador_ram));  // open: sel
  ROM #(.addrWidth(3), .dataWidth(7)) rom_1 (.addr(counter_1_q), .data(rom_1_data));  // open: sel
  or or_2 (zera, in_6, zera_oi);
  Comparator #(.width(7)) comparator_3 (.a(out_7), .b(7'b0001010), .eq(comparator_3_eq));  // open: gt, lt
  Counter #(.width(2), .max('h3), .ongoal("stay")) counter_3 (
    .Q(counter_3_q), .clk(comparator_4_eq), .clr(zera));  // open: load, D, count, carry
  Comparator #(.width(7)) comparator_4 (.a(saidaRam2), .b(rom_1_data), .eq(comparator_4_eq));  // open: gt, lt
  Comparator #(.width(7)) comparator_5 (.a(oi), .b({7{1'b0}}), .eq(comparator_5_eq));  // open: gt, lt
  Register #(.width(1)) register_1 (
    .D(comparator_3_eq), .Q(register_1_q), .clk(comparator_3_eq), .clr(zera));  // open: en
  Comparator #(.width(2)) comparator_6 (.a(2'b11), .b(counter_3_q), .eq(comparator_6_eq));  // open: gt, lt
  Clock clock_2 (.out(clock_2_out));
  Multiplexer #(.width(7), .enable("false")) multiplexer_2 (
    .in1(out_7), .out(saidaRam2), .sel(register_1_q));  // open: in0
  and and_3 (and_3_out, comparator_5_eq, zera_oi);
  Register #(.width(1)) register_2 (
    .D(comparator_6_eq), .Q(verifica_oi), .clk(comparator_6_eq), .clr(or_3_out));  // open: en
  and and_4 (and_4_out, verifica_oi, and_3_out);
  and and_5 (and_5_out, verifica_oi, clock_2_out);
  or or_3 (or_3_out, zera, and_4_out);
  Counter #(.width(3), .max('h4), .ongoal("stay")) counter_4 (
    .Q(teste), .clk(and_5_out), .clr(zera));  // open: load, D, count, carry
  Comparator #(.width(7)) comparator_7 (.a({7{1'b0}}), .b(rom_2_data), .eq(zera_oi));  // open: gt, lt
  ROM #(.addrWidth(3), .dataWidth(7)) rom_2 (.addr(teste), .data(rom_2_data));  // open: sel
  Multiplexer #(.width(7), .enable("false")) multiplexer_3 (.in0(rom_2_data), .out(oi), .sel(zera_oi));  // open: in1

  // Other names for the same wires on the sheet: input[6:0] = out_8; saida_RAM[6:0] = out_7;
  //   zera_o_clock_oi = verifica_oi

  // Notes on the sheet:
  //   contents of rom_1 (hex, n*v repeats v):
  //   6f 69 a
  //   Zera os clocks
  //   Respostas do bot
  //   contents of rom_2 (hex, n*v repeats v):
  //   11 6f 69 a
endmodule
